# Fritzing sketch wiring (saved by Fritzing 0.9.0b)
breadboards: 1

parts:
  Деталь1 = Arduino Nano (Rev3.0)
  RHT1 = Humidity and Temperature Sensor RHT03
  Деталь2 = Barometric Pressure Sensor - BMP085 Breakout
  TRXCOM1 = RJ45-TRXCOM [part_number=TRJ0011BANL]  # not connected
  JP2 = Header 10 [package=1x10-2mm-smd]
  R1 = Resistor [tolerance=±5% resistance=1k package=THT]

nets:
  GND: Деталь1.GND, RHT1.GND_2, Деталь2.GND, JP2.GND
  N1: Деталь1.D3, RHT1.Data-signal, R1.Pin_1
  N2: Деталь1.D5, JP2.RST
  N3: Деталь1.D8, JP2.CS
  N4: Деталь1.D11/MOSI, JP2.SI
  N5: Деталь1.D12/MISO, JP2.SO
  5V: Деталь1.5V, RHT1.Vcc, R1.Pin_0
  N6: Деталь1.A5, Деталь2.SCL
  N7: Деталь1.A4, Деталь2.SDA
  VCC: Деталь1.3V3, Деталь2.VCC, JP2.VCC
  N8: Деталь1.D13/SCK, JP2.SCK

notes:
  ENC28J60 LAN module

custom parts:
  Header 10: Header 10 Standard 10-pin 0.1 header. Use with straight break away headers (SKU : PRT-00116), right angle break away headers (PRT-00553), swiss pins (PRT-00743), machine pins (PRT-00117), and female headers (PRT-00115).
